# Fritzing sketch CombinatorialCircuit1 (saved by Fritzing 0.9.1b)
circuit board: 8.46667cm x 5.64444cm
breadboards: 1

parts:
  IC2 = 74HCT08 [package="DIP (Dual Inline) [THT]"]
  IC3 = 74HCT32 [package="DIP (Dual Inline) [THT]"]
  J1 = female pin header, 1 pin [form="♀ (female)"]
  J2 = female pin header, 1 pin [form="♀ (female)"]
  SW1 = DIP SW-3 [package="DIP (Dual Inline) [THT]"]
  LED4 = Yellow LED 3mm 5V
  LED5 = Red LED 3mm 5V
  LED1 = Green LED 3mm 5V
  LED2 = Green LED 3mm 5V
  LED3 = Green LED 3mm 5V
  IC4 = 74HCT00 [package="DIP (Dual Inline) [THT]"]

nets:
  GND: IC2.GND, IC3.GND, J2.pin1, LED4.pin2, LED5.pin2, LED1.pin2, LED2.pin2, LED3.pin2, IC4.GND
  VCC: IC2.Vcc, IC3.Vcc, J1.pin1, SW1.4, SW1.5, SW1.6, IC4.Vcc
  N1: SW1.1, LED1.pin1
  N2: SW1.2, LED2.pin1
  N3: SW1.3, LED3.pin1

custom parts:
  74HCT08: Quad 2 input AND gates
  74HCT32: Quad 2 input OR gates
  DIP SW-3: 3 DIP switches
  Yellow LED 3mm 5V: LED with internal resistor 5V
  Red LED 3mm 5V: LED with internal resistor 5V
  Green LED 3mm 5V: LED with internal resistor 5V
  74HCT00: Quad 2 input NAND gates
